// Logisim project circuito.circ as structural Verilog: 2 circuits, main circuit main
module main (
  input  in_1,
  input  in_2,
  input  in_3,
  input  in_4
);

  wire decodificadorbcddisplay7seg_1_a, decodificadorbcddisplay7seg_1_b, decodificadorbcddisplay7seg_1_c,
       decodificadorbcddisplay7seg_1_d, decodificadorbcddisplay7seg_1_e, decodificadorbcddisplay7seg_1_f,
       decodificadorbcddisplay7seg_1_g, decodificadorbcddisplay7seg_1_out_12;

  DecodificadorBCDDisplay7Seg decodificadorbcddisplay7seg_1 (
    .d3(in_1), .d2(in_2), .d1(in_3), .d0(in_4), .a(decodificadorbcddisplay7seg_1_a),
    .b(decodificadorbcddisplay7seg_1_b), .c(decodificadorbcddisplay7seg_1_c),
    .d(decodificadorbcddisplay7seg_1_d), .e(decodificadorbcddisplay7seg_1_e),
    .f(decodificadorbcddisplay7seg_1_f), .g(decodificadorbcddisplay7seg_1_g),
    .out_12(decodificadorbcddisplay7seg_1_out_12));
  _7_Segment_Display u_7_segment_display_1 (
    .g(decodificadorbcddisplay7seg_1_g), .f(decodificadorbcddisplay7seg_1_f),
    .a(decodificadorbcddisplay7seg_1_a), .b(decodificadorbcddisplay7seg_1_b),
    .e(decodificadorbcddisplay7seg_1_e), .d(decodificadorbcddisplay7seg_1_d),
    .c(decodificadorbcddisplay7seg_1_c));  // open: dp
  LED led_1 (.in(decodificadorbcddisplay7seg_1_out_12));
endmodule

module DecodificadorBCDDisplay7Seg (
  input  d3,
  input  d2,
  input  d1,
  input  d0,
  output a,
  output b,
  output c,
  output d,
  output e,
  output f,
  output g,
  output out_12
);

  wire and_1_out, and_2_out, and_3_out, and_4_out, and_5_out, and_6_out, and_7_out, and_8_out, and_9_out,
       and_10_out, and_11_out, and_12_out, and_13_out, and_14_out, and_15_out, and_16_out, and_17_out,
       and_18_out, and_19_out, and_20_out, and_21_out, and_22_out, and_23_out, and_24_out, and_25_out,
       and_26_out, and_27_out, and_28_out, not_1_out, not_2_out, not_3_out, not_4_out;

  not not_1 (not_1_out, d3);
  not not_2 (not_2_out, d2);
  not not_3 (not_3_out, d1);
  not not_4 (not_4_out, d0);
  and and_1 (and_1_out, not_1_out, d1);
  and and_2 (and_2_out, not_1_out, d2, d0);
  and and_3 (and_3_out, d3, not_2_out, not_3_out);
  and and_4 (and_4_out, not_1_out, not_2_out, not_4_out);
  and and_5 (and_5_out, not_1_out, not_2_out);
  and and_6 (and_6_out, not_1_out, not_3_out, not_4_out);
  and and_7 (and_7_out, not_1_out, d1, d0);
  and and_8 (and_8_out, not_2_out, not_3_out);
  and and_9 (and_9_out, not_1_out, d0);
  and and_10 (and_10_out, not_1_out, d2);
  and and_11 (and_11_out, not_2_out, not_3_out);
  and and_12 (and_12_out, not_1_out, not_2_out, d1);
  and and_13 (and_13_out, not_1_out, d2, not_3_out, d0);
  and and_14 (and_14_out, not_1_out, d1, not_4_out);
  and and_15 (and_15_out, d3, not_2_out, not_3_out);
  and and_16 (and_16_out, not_1_out, not_2_out, not_4_out);
  and and_17 (and_17_out, not_1_out, d1, not_4_out);
  and and_18 (and_18_out, not_2_out, not_3_out, not_4_out);
  and and_19 (and_19_out, not_1_out, d2, not_3_out);
  and and_20 (and_20_out, not_1_out, d2, not_4_out);
  and and_21 (and_21_out, d3, not_2_out, not_3_out);
  and and_22 (and_22_out, not_1_out, not_3_out, not_4_out);
  and and_23 (and_23_out, not_1_out, not_2_out, d1);
  and and_24 (and_24_out, not_1_out, d2, not_3_out);
  and and_25 (and_25_out, d3, not_2_out, not_3_out);
  and and_26 (and_26_out, not_1_out, d1, not_4_out);
  and and_27 (and_27_out, d3, d1);
  and and_28 (and_28_out, d3, d2);
  or or_1 (a, and_1_out, and_2_out, and_3_out, and_4_out);
  or or_2 (b, and_5_out, and_6_out, and_7_out, and_8_out);
  or or_3 (c, and_9_out, and_10_out, and_11_out);
  or or_4 (d, and_12_out, and_13_out, and_14_out, and_15_out, and_16_out);
  or or_5 (e, and_17_out, and_18_out);
  or or_6 (f, and_19_out, and_20_out, and_21_out, and_22_out);
  or or_7 (g, and_23_out, and_24_out, and_25_out, and_26_out);
  or or_8 (out_12, and_27_out, and_28_out);
endmodule
